# Fritzing sketch dht11toserial (saved by Fritzing 0.9.3b)
breadboards: 1

parts:
  DHT1 = DHT11 Humitidy and Temperature Sensor
  Part1 = Arduino Nano (Rev3.0) (ICSP)

nets:
  VDD: DHT1.VDD, Part1.5V
  N1: DHT1.DATA, Part1.D11/MOSI
  GND: DHT1.GND, Part1.GND

custom parts:
  DHT11 Humitidy and Temperature Sensor: DHT11 Humidity and Temperature Sensor
